// Logisim project PipelinedProcessor.circ as structural Verilog: 1 circuit, main circuit main
module main (
);

  wire ALUSrc, clk, DisableIR, DisablePC, JumpOP, MemoryRead, MemoryWrite, not_1_out, not_2_out, not_3_out,
       RegWrite, signExtend, SLT, undriven_5, ZeroFlag;
  wire [1:0] BranchOP, F, PCSrc, RegDest, RegisterWSrc, undriven_3, undriven_8;
  wire [2:0] multiplexer_2_out, Rd, Rs, Rt, undriven;
  wire [3:0] ALUop;
  wire [4:0] Imm5, Opcode;
  wire [5:0] ExecutionSignals_q;
  wire [10:0] Imm11;
  wire [15:0] BranchPC, IR, JumpPC, multiplexer_1_out, OperandA, OperandB, PC, PC_1, R1, R2, R3, R4, R5, R6,
       R7, RegisterWrite, ReturnAdress, rom_1_data, undriven_2, undriven_4, undriven_6, undriven_7;

  // Probe on PCSrc
  Multiplexer #(.select(2), .width(16), .enable("false")) multiplexer_1 (
    .in0({16{1'b0}}), .in1(BranchPC), .in2(JumpPC), .in3(PC_1), .out(multiplexer_1_out), .sel(PCSrc));
  Register #(.width(16)) register_1 (.D(multiplexer_1_out), .Q(PC), .clk(clk));  // open: en, clr
  Adder #(.width(16)) adder_1 (.a(16'h1), .b(PC), .out(PC_1), .cin(1'b0));  // open: cout
  ControlUnit controlunit_1 (
    .Opcode(Opcode), .Function(F), .ALUop(ALUop), .ALUSrc(ALUSrc), .signExtend(signExtend),
    .RegWrite(RegWrite), .RegDest(RegDest), .RegWSrc(RegisterWSrc), .memoryRead(MemoryRead),
    .memoryWrite(MemoryWrite), .PCSrc(PCSrc), .BrachOP(BranchOP), .JumpOP(JumpOP));
  Clock clock_1 (.out(clk));
  ROM #(.addrWidth(16), .dataWidth(16)) rom_1 (.addr(PC), .data(rom_1_data), .sel(1'b1));
  Register #(.width(16)) PCRegister (.D(PC_1), .en(not_1_out), .Q(ReturnAdress), .clk(clk));  // open: clr
  not not_1 (not_1_out, DisablePC);
  Register #(.width(16)) InstructionRegister (.D(rom_1_data), .en(not_2_out), .Q(IR), .clk(clk));  // open: clr
  not not_2 (not_2_out, DisableIR);
  // Probe on BranchOP
  InstructionSplitter instructionsplitter_1 (
    .Instruction(IR), .Op(Opcode), .F(F), .Rd(Rd), .Rs(Rs), .Rt(Rt), .Imm5(Imm5), .Imm11(Imm11));
  // Probe on Opcode
  // JumpControl jumpcontrol_1: pin names not known; wires that end beside it: PC, OperandA, Imm11, JumpOP, JumpPC
  // Probe on Imm5
  // Probe on Rs
  // Probe on Rt
  // Probe on Rd
  BranchControl branchcontrol_1 (
    .Operation(BranchOP), .Zero(ZeroFlag), .Less_Than(SLT), .Imm5(Imm5), .PC(PC), .newPC(BranchPC));
  Multiplexer #(.select(2), .width(3), .enable("false")) multiplexer_2 (
    .in0(Rt), .in1(undriven), .in2(3'b001), .in3(3'b111), .out(multiplexer_2_out), .sel(undriven_3));
  RegisterFile registerfile_1 (
    .Reg_Write(undriven_5), .CLK(clk), .RA(Rs), .RB(Rt), .RW(multiplexer_2_out), .Bus_W(RegisterWrite),
    .Bus_A(OperandA), .Bus_B(OperandB), .R1(R1), .R2(R2), .R3(R3), .R4(R4), .R5(R5), .R6(R6), .R7(R7));
  Multiplexer #(.select(2), .width(16), .enable("false")) multiplexer_3 (
    .in0(undriven_7), .in1(undriven_6), .in2(undriven_4), .in3(undriven_2), .out(RegisterWrite),
    .sel(undriven_8));
  Register #(.width(16)) PCRegister_2 (.D(PC_1), .en(not_3_out), .clk(clk));  // open: Q, clr
  not not_3 (not_3_out, DisablePC);
  Register #(.width(11)) u_imm11 (.D(Imm11), .clk(clk));  // open: en, Q, clr
  Register #(.width(5)) u_imm5 (.D(Imm5), .clk(clk));  // open: en, Q, clr
  Register #(.width(16)) RsValueRegister (.D(OperandA), .clk(clk));  // open: en, Q, clr
  Register #(.width(16)) RtValueRegister (.D(OperandB), .clk(clk));  // open: en, Q, clr
  Register #(.width(3)) Rd2 (.D(Rd), .clk(clk));  // open: en, Q, clr
  Register #(.width(6)) ExecutionSignals (
    .D({signExtend, ALUSrc, ALUop}), .Q(ExecutionSignals_q), .clk(clk));  // open: en, clr
  Register #(.width(5)) WriteBackSignals (.D({RegWrite, RegDest, RegisterWSrc}), .clk(clk));  // open: en, Q, clr
  Register #(.width(2)) MemorySignals (.D({MemoryRead, MemoryWrite}), .clk(clk));  // open: en, Q, clr

  // Other names for the same wires on the sheet: RsValue[15:0] = OperandA; RtValue[15:0] = OperandB

  // Notes on the sheet:
  //   contents of rom_1 (hex, n*v repeats v):
  //   9000 280b 97ff 2fca 681a 840 880 8c0 6001 9808 9bc8 f000
  //   IF/ID Register
endmodule
